# Fritzing sketch enviromon (saved by Fritzing 0.9.4)

parts:
  Part1 = Adafruit Pro Trinket 3.3V 12MHz [part_number="Adafruit #2010"]
  ZS-042_RTC1 = ZS-042 RTC Module
  DHT1 = DHT11 Humitidy and Temperature Sensor
  DS1 = DS18B20 1-Wire Temperature Sensor [part_number=DS18B20]
  BAT1 = Battery Holders [package=lipo-1100mAh]
  S1 = Pushbutton [package=THT]
  U1 = SWITCH_SPDT [package=kps-1290]
  C1 = Ceramic Capacitor [capacitance=10nF package="200 mil [THT, multilayer]"]
  R1 = Resistor [tolerance=±5% resistance=330k package="0603 [SMD]"]
  R2 = Resistor [tolerance=±5% resistance=330k package="0603 [SMD]"]
  R3 = Resistor [tolerance=±5% resistance=4.7k package="0603 [SMD]"]
  R4 = Resistor [tolerance=±5% resistance=4.7k package="0603 [SMD]"]

nets:
  GND: Part1.GND, Part1.A1, ZS-042_RTC1.GND, DHT1.GND, DS1.GND, BAT1.-, S1.leg1, U1.O, C1.1, R2.Pin_1
  N1: Part1.VBAT, BAT1.+, R1.Pin_0
  VDD: Part1.+3V3, ZS-042_RTC1.VCC, DHT1.VDD, DS1.VDD, U1.S, R3.Pin_0, R4.Pin_1
  N2: Part1.D8, U1.P
  N3: Part1.D6, DS1.DQ, R3.Pin_1
  N4: Part1.D5, DHT1.DATA, R4.Pin_0
  N5: Part1.D3, ZS-042_RTC1.SQW
  N6: Part1.A4, ZS-042_RTC1.SDA
  N7: Part1.A5, ZS-042_RTC1.SCL
  N8: C1.0, R2.Pin_0

custom parts:
  Adafruit Pro Trinket 3.3V 12MHz: rinket's got a big sister in town - the Pro Trinket 3V! Pro Trinket combines everything you love about Trinket with the familiarity of the core Arduino chip, the ATmega328. It's like an Arduino Pro Mini with more pins and USB tossed in. Trinket's a year old now, and while its been great to see tons of tiny projects, sometimes you just need more pins, more FLASH, and more RAM. That's why we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
  DHT11 Humitidy and Temperature Sensor: DHT11 Humidity and Temperature Sensor
